# Fritzing sketch nodemcu-buttons-wifi-batmon (saved by Fritzing 0.9.3b)
breadboards: 1

parts:
  S2 = Round Pushbutton
  BAT1 = BC9VPC [package=bc9vpc]
  U1 = NodeMCU V1.0
  LED1 = smd LED [color="Red (633nm)" package="1206 [SMD]"]
  R1 = Resistor [tolerance=±5% resistance=22k package="0805 [SMD]"]
  R2 = Resistor [tolerance=±5% resistance=470 package="0805 [SMD]"]
  R3 = Resistor [tolerance=±5% resistance=22k package="0805 [SMD]"]
  R4 = Resistor [tolerance=±5% resistance=330k package="0805 [SMD]"]

nets:
  N1: S2.leg0, U1.3V3, R1.Pin_0
  N2: S2.leg1, BAT1.V-, U1.GND, LED1.cathode, R3.Pin_0
  N3: BAT1.V+, U1.Vin, R2.Pin_0, R4.Pin_1
  N4: U1.D1, R1.Pin_1
  N5: U1.A0, R3.Pin_1, R4.Pin_0
  N6: LED1.anode, R2.Pin_1

notes:
  place NodeMCU near to the buttons (few meters)
  instead of 9V battery you can use power supply from 6V to 12V
  red wire = 6V to 12V
  orange wire = 3.3V
  green wire = max. 1V
  take care for the right resistor on LED corresponding to ypur battery voltage

custom parts:
  NodeMCU V1.0: ESP8266 based NodeMCU
